# Fritzing sketch schemat (saved by Fritzing 0.9.3b)

parts:
  S1 = H-Bridge with L298N
  M1 = DC Motor
  M2 = DC Motor
  VCC2 = 4 x AAA Battery Mount  # not connected
  Part1 = Arduino Uno (Rev3)  # not connected
  Part2 = Bluetooth HC-05 Macho  # not connected
  Part3 = Logic Level Converter  # not connected
  M3 = DC Motor  # not connected
  M4 = DC Motor  # not connected
  VCC1 = 4 x AAA Battery Mount  # not connected

nets:
  N1: S1.M1-01, M1.pin_2
  N2: S1.M1-02, M1.pin_1
  N3: S1.M2-01, M2.pin_2
  N4: S1.M2-02, M2.pin_1

custom parts:
  H-Bridge with L298N: h-bridge
